# Fritzing sketch ESP32-TTGO-T7-OctalCTSense (saved by Fritzing 0.9.5d)
perfboards: 1

parts:
  TTGO-T7_V1_4 = TTGO-T7 V1.3 [part_number=TTGO-T7-V1.3]
  J5 = Screw terminal - 2 pins [package=THT]
  J6 = Screw terminal - 2 pins [package=THT]
  D4 = Schottky Diode [part_number=SB240E package="300 mil [THT]"]
  D5 = Schottky Diode [part_number=SB240E package="300 mil [THT]"]
  D6 = Schottky Diode [part_number=SB240E package="300 mil [THT]"]
  Part5 = prefix0000
  Part6 = prefix0000
  R3 = Resistor [package=THT]
  R4 = Resistor [package=THT]
  J7 = double row male pin header, 2 pins [form="♂ (male)"]
  J8 = double row male pin header, 2 pins [form="♂ (male)"]
  C6 = Capacitor [part_number=.1nf package=axial-5mm]
  C7 = Capacitor [part_number=47nf package=axial-5mm]
  IC3 = IC, DIP package, 8 pins [chip_label=TCAN332DR]
  C8 = Electrolytic Capacitor [capacitance=1µF package="100 mil [THT, electrolytic]"]
  IC4 = IC, DIP package, 8 pins [chip_label=LM2574N-5.0]
  C9 = Tantalum Capacitor [capacitance=22µF voltage=0.1kV package="200 mil [THT, tantalum]"]
  C10 = Tantalum Capacitor [capacitance=0.22mF voltage=35V package="200 mil [THT, tantalum]"]
  L2 = Inductors [package=npi75c]
  J9 = screw terminal, 8 pins
  D7 = Diode [package=diode-1n4148]
  D8 = Diode [package=diode-1n4148]
  D9 = Diode [package=diode-1n4148]
  D10 = Diode [package=diode-1n4148]
  D11 = Diode [package=diode-1n4148]
  D12 = Diode [package=diode-1n4148]
  D13 = Diode [package=diode-1n4148]
  D14 = Diode [package=diode-1n4148]
  U1 = Quad Comparator [part_number=LM339 package="DIP (Dual Inline) [THT]"]  # not connected
  part = Quad Comparator [part_number=LM339 package="DIP (Dual Inline) [THT]"]
  U1_1 = Quad Comparator [part_number=LM339 package="DIP (Dual Inline) [THT]"]
  U1_2 = Quad Comparator [part_number=LM339 package="DIP (Dual Inline) [THT]"]
  U1_3 = Quad Comparator [part_number=LM339 package="DIP (Dual Inline) [THT]"]
  U1_4 = Quad Comparator [part_number=LM339 package="DIP (Dual Inline) [THT]"]
  U2 = Quad Comparator [part_number=LM339 package="DIP (Dual Inline) [THT]"]  # not connected
  part_2 = Quad Comparator [part_number=LM339 package="DIP (Dual Inline) [THT]"]
  U2_1 = Quad Comparator [part_number=LM339 package="DIP (Dual Inline) [THT]"]
  U2_2 = Quad Comparator [part_number=LM339 package="DIP (Dual Inline) [THT]"]
  U2_3 = Quad Comparator [part_number=LM339 package="DIP (Dual Inline) [THT]"]
  U2_4 = Quad Comparator [part_number=LM339 package="DIP (Dual Inline) [THT]"]
  R5 = Resistor [tolerance=±5% resistance=22k package=THT]
  R6 = Trimmer Potentiometer [maximum_resistance=10kΩ package=THT]
  R7 = Resistor [tolerance=±5% resistance=1M package=THT]
  C11 = Electrolytic Capacitor [capacitance=2.2µF package="100 mil [THT, electrolytic]"]
  LED1 = LED - 3mm [color="Red (633nm)" package="3 mm [THT]"]
  R8 = Resistor [tolerance=±5% resistance=3.3k package=THT]
  R9 = Trimmer Potentiometer [maximum_resistance=10kΩ package=THT]
  R10 = Trimmer Potentiometer [maximum_resistance=10kΩ package=THT]
  R11 = Trimmer Potentiometer [maximum_resistance=10kΩ package=THT]
  R12 = Resistor [tolerance=±5% resistance=22k package=THT]
  R13 = Resistor [tolerance=±5% resistance=22k package=THT]
  R14 = Resistor [tolerance=±5% resistance=22k package=THT]
  R15 = Resistor [tolerance=±5% resistance=1M package=THT]
  R16 = Resistor [tolerance=±5% resistance=1M package=THT]
  R17 = Resistor [tolerance=±5% resistance=1M package=THT]
  C12 = Electrolytic Capacitor [capacitance=2.2µF package="100 mil [THT, electrolytic]"]
  C13 = Electrolytic Capacitor [capacitance=2.2µF package="100 mil [THT, electrolytic]"]
  C14 = Electrolytic Capacitor [capacitance=2.2µF package="100 mil [THT, electrolytic]"]
  LED2 = LED - 3mm [color="Red (633nm)" package="3 mm [THT]"]
  LED3 = LED - 3mm [color="Red (633nm)" package="3 mm [THT]"]
  LED4 = LED - 3mm [color="Red (633nm)" package="3 mm [THT]"]
  R18 = Resistor [tolerance=±5% resistance=3.3k package=THT]
  R19 = Resistor [tolerance=±5% resistance=3.3k package=THT]
  R20 = Resistor [tolerance=±5% resistance=3.3k package=THT]

nets (from the schematic view):
  GND: TTGO-T7_V1_4.GND1, TTGO-T7_V1_4.GND2, TTGO-T7_V1_4.GND3, J5.pin2, J6.pin2, D5.anode, Part5.N$3, Part5.N$5, Part5.N$6, Part6.N$3, Part6.N$5, Part6.N$6, C6.2, C7.1, IC3.pin2, C8.-, IC4.pin2, IC4.pin3, IC4.pin4, C9.-, C10.-, part.pin_12, part_2.pin_12, R6.leg2, C11.-, R9.leg2, R10.leg2, R11.leg2, C12.-, C13.-, C14.-
  LED 3: TTGO-T7_V1_4.IO_36
  LED 4: TTGO-T7_V1_4.IO_39
  Button 3: TTGO-T7_V1_4.IO_26
  LED 2: TTGO-T7_V1_4.IO_35
  OD 5: TTGO-T7_V1_4.IO_18
  OD 8: TTGO-T7_V1_4.IO_33
  OD 6: TTGO-T7_V1_4.IO_19
  LED 1: TTGO-T7_V1_4.IO_34
  Button 1: TTGO-T7_V1_4.IO_23
  CAN TX: TTGO-T7_V1_4.IO_05, IC3.pin1
  3.3V: TTGO-T7_V1_4.3V3, C6.1, IC3.pin3, C8.+, part.pin_3, part_2.pin_3, R5.Pin_0, R7.Pin_0, R8.Pin_0, R12.Pin_0, R13.Pin_0, R14.Pin_0, R15.Pin_0, R16.Pin_0, R17.Pin_0, R18.Pin_0, R19.Pin_0, R20.Pin_0
  Button 4: TTGO-T7_V1_4.IO_27
  Button 2: TTGO-T7_V1_4.IO_25
  OD 7: TTGO-T7_V1_4.IO_32
  OD 4: TTGO-T7_V1_4.IO_17, U2_3.pin_14, LED4.cathode
  OD 3: TTGO-T7_V1_4.IO_16, U2_4.pin_13, LED3.cathode
  CAN RX: TTGO-T7_V1_4.IO_04, IC3.pin4
  OD 1: TTGO-T7_V1_4.IO_00, U2_2.pin_2, LED1.cathode
  5V: TTGO-T7_V1_4.+5V, IC4.pin1, C10.+, L2.2
  OD 2: TTGO-T7_V1_4.IO_02, U2_1.pin_1, LED2.cathode
  N1: J5.pin1, D6.anode
  N2: J6.pin1, D4.cathode
  12V: D4.anode, D6.cathode, Part5.N$8, Part6.N$8, IC4.pin5, C9.+
  N3: D5.cathode, IC4.pin7, L2.1
  CAN H: Part5.N$1, Part6.N$1, R3.Pin_0, IC3.pin7
  CAN L: Part5.N$2, Part6.N$2, R4.Pin_0, IC3.pin6
  N4: Part5.N$4, Part6.N$4
  N5: Part5.N$7, Part6.N$7
  N6: R3.Pin_1, J7.pin2
  N7: R4.Pin_1, J8.pin2
  N8: J7.pin1, J8.pin1, C7.2
  N9: J9.pin1, D7.A, D8.C, U1_2.pin_4
  N10: J9.pin2, D7.C, D8.A, R6.wiper
  N11: J9.pin3, D9.A, D10.C, U1_1.pin_6
  N12: J9.pin4, D9.C, D10.A, R9.wiper
  N13: J9.pin5, D12.A, D13.C, U1_4.pin_10#9
  N14: J9.pin6, D12.C, D13.A, R10.wiper
  N15: J9.pin7, D11.A, D14.C, U1_3.pin_8
  N16: J9.pin8, D11.C, D14.A, R11.wiper
  N17: U1_1.pin_1, U2_1.pin_7, R15.Pin_1, C12.+
  N18: U1_1.pin_7, U2_1.pin_6, R9.leg1, R12.Pin_1
  N19: U1_2.pin_2, U2_2.pin_5, R7.Pin_1, C11.+
  N20: U1_2.pin_5, U2_2.pin_4, R5.Pin_1, R6.leg1
  N21: U1_3.pin_9, U2_3.pin_8, R11.leg1, R14.Pin_1
  N22: U1_3.pin_14, U2_3.pin_9, R17.Pin_1, C14.+
  N23: U1_4.pin_10#10, U2_4.pin_10#9, R10.leg1, R13.Pin_1
  N24: U1_4.pin_13, U2_4.pin_10#10, R16.Pin_1, C13.+
  N25: LED1.anode, R8.Pin_1
  N26: LED2.anode, R18.Pin_1
  N27: LED3.anode, R19.Pin_1
  N28: LED4.anode, R20.Pin_1

custom parts:
  Resistor: A generic 5-band resistor (0.25W)
  Quad Comparator: LM239 Quad Comparator
  Quad Comparator: LM239 Quad Comparator
  Quad Comparator: LM239 Quad Comparator
  Quad Comparator: LM239 Quad Comparator
  Quad Comparator: LM239 Quad Comparator
  Quad Comparator: LM239 Quad Comparator
